// Digital circuit 1_bit.dig as structural Verilog
module _1_bit (
  input  clk,
  input  load,
  input  in,
  output out
);

  wire multiplexer_1_out;

  Multiplexer multiplexer_1 (.sel(load), .in_0(out), .in_1(in), .out(multiplexer_1_out));
  D_FF d_ff_1 (.D(multiplexer_1_out), .C(clk), .Q(out));  // open: nQ
endmodule
