// Digital circuit 4wayDemux.dig as structural Verilog
module _4wayDemux (
  input  in,
  input  [1:0] sel,
  output a,
  output b,
  output c,
  output d
);

  wire demultiplexer_1_out_0, demultiplexer_1_out_1;

  Demultiplexer demultiplexer_1 (.sel(sel[1]), .in(in), .out_0(demultiplexer_1_out_0), .out_1(demultiplexer_1_out_1));
  Demultiplexer demultiplexer_2 (.sel(sel[0]), .in(demultiplexer_1_out_0), .out_0(a), .out_1(b));
  Demultiplexer demultiplexer_3 (.sel(sel[0]), .in(demultiplexer_1_out_1), .out_0(c), .out_1(d));
endmodule
