// Digital circuit 4waymux16.dig as structural Verilog
module _4waymux16 (
  input  [15:0] a,
  input  [15:0] b,
  input  [15:0] c,
  input  [15:0] d,
  input  [1:0] sel,
  output [15:0] out
);

  wire [15:0] mux16_1_out, mux16_2_out;

  mux16 mux16_1 (.a(a), .b(b), .sel(sel[0]), .out(mux16_1_out));
  mux16 mux16_2 (.a(c), .b(d), .sel(sel[0]), .out(mux16_2_out));
  mux16 mux16_3 (.a(mux16_1_out), .b(mux16_2_out), .sel(sel[1]), .out(out));
endmodule
