// Digital circuit 8wayDmux.dig as structural Verilog
module _8wayDmux (
  input  in,
  input  [2:0] sel,
  output a,
  output b,
  output c,
  output d,
  output e,
  output f,
  output g,
  output h
);

  wire demultiplexer_1_out_0, demultiplexer_1_out_1;

  Demultiplexer demultiplexer_1 (.sel(sel[2]), .in(in), .out_0(demultiplexer_1_out_0), .out_1(demultiplexer_1_out_1));
  _4wayDemux _4waydemux_1 (.in(demultiplexer_1_out_0), .sel(sel[1:0]), .a(a), .b(b), .c(c), .d(d));
  _4wayDemux _4waydemux_2 (.in(demultiplexer_1_out_1), .sel(sel[1:0]), .a(e), .b(f), .c(g), .d(h));
endmodule
