// Digital circuit 8waymux16.dig as structural Verilog
module _8waymux16 (
  input  [15:0] a,
  input  [15:0] b,
  input  [15:0] c,
  input  [15:0] d,
  input  [15:0] e,
  input  [15:0] f,
  input  [15:0] g,
  input  [15:0] h,
  input  [2:0] sel,
  output [15:0] out
);

  wire [15:0] _4waymux16_1_out, _4waymux16_2_out;

  _4waymux16 _4waymux16_1 (.a(a), .b(b), .c(c), .d(d), .sel(sel[1:0]), .out(_4waymux16_1_out));
  _4waymux16 _4waymux16_2 (.a(e), .b(f), .c(g), .d(h), .sel(sel[1:0]), .out(_4waymux16_2_out));
  mux16 mux16_1 (.a(_4waymux16_1_out), .b(_4waymux16_2_out), .sel(sel[2]), .out(out));
endmodule
