// Digital circuit Half_adder.dig as structural Verilog
module Half_adder (
  input  a,
  input  b,
  output carry,
  output sum
);

  wire and_2_out, and_3_out, not_1_out, not_2_out;

  not not_1 (not_1_out, a);
  not not_2 (not_2_out, b);
  and and_1 (carry, a, b);
  and and_2 (and_2_out, not_1_out, b);
  and and_3 (and_3_out, not_2_out, a);
  or or_1 (sum, and_2_out, and_3_out);
endmodule
