// Digital circuit adder_16.dig as structural Verilog
module adder_16 (
  input  [15:0] a,
  input  [15:0] b,
  output [15:0] sum
);

  wire full_adder_1_carry, full_adder_2_carry, full_adder_3_carry, full_adder_4_carry, full_adder_5_carry,
       full_adder_6_carry, full_adder_7_carry, full_adder_8_carry, full_adder_9_carry, full_adder_10_carry,
       full_adder_11_carry, full_adder_12_carry, full_adder_13_carry, full_adder_14_carry,
       full_adder_15_carry;

  full_adder full_adder_1 (.a(a[0]), .b(b[0]), .c(1'b0), .sum(sum[0]), .carry(full_adder_1_carry));
  full_adder full_adder_2 (.a(a[1]), .b(b[1]), .c(full_adder_1_carry), .sum(sum[1]), .carry(full_adder_2_carry));
  full_adder full_adder_3 (.a(a[2]), .b(b[2]), .c(full_adder_2_carry), .sum(sum[2]), .carry(full_adder_3_carry));
  full_adder full_adder_4 (.a(a[3]), .b(b[3]), .c(full_adder_3_carry), .sum(sum[3]), .carry(full_adder_4_carry));
  full_adder full_adder_5 (.a(a[4]), .b(b[4]), .c(full_adder_4_carry), .sum(sum[4]), .carry(full_adder_5_carry));
  full_adder full_adder_6 (.a(a[5]), .b(b[5]), .c(full_adder_5_carry), .sum(sum[5]), .carry(full_adder_6_carry));
  full_adder full_adder_7 (.a(a[6]), .b(b[6]), .c(full_adder_6_carry), .sum(sum[6]), .carry(full_adder_7_carry));
  full_adder full_adder_8 (.a(a[7]), .b(b[7]), .c(full_adder_7_carry), .sum(sum[7]), .carry(full_adder_8_carry));
  full_adder full_adder_9 (.a(a[8]), .b(b[8]), .c(full_adder_8_carry), .sum(sum[8]), .carry(full_adder_9_carry));
  full_adder full_adder_10 (.a(a[9]), .b(b[9]), .c(full_adder_9_carry), .sum(sum[9]), .carry(full_adder_10_carry));
  full_adder full_adder_11 (.a(a[10]), .b(b[10]), .c(full_adder_10_carry), .sum(sum[10]), .carry(full_adder_11_carry));
  full_adder full_adder_12 (.a(a[11]), .b(b[11]), .c(full_adder_11_carry), .sum(sum[11]), .carry(full_adder_12_carry));
  full_adder full_adder_13 (.a(a[12]), .b(b[12]), .c(full_adder_12_carry), .sum(sum[12]), .carry(full_adder_13_carry));
  full_adder full_adder_14 (.a(a[13]), .b(b[13]), .c(full_adder_13_carry), .sum(sum[13]), .carry(full_adder_14_carry));
  full_adder full_adder_15 (.a(a[14]), .b(b[14]), .c(full_adder_14_carry), .sum(sum[14]), .carry(full_adder_15_carry));
  full_adder full_adder_16 (.a(a[15]), .b(b[15]), .c(full_adder_15_carry), .sum(sum[15]));  // open: carry
endmodule
