// Digital circuit alu.dig as structural Verilog
module alu (
  input  zx,
  input  nx,
  input  f,
  input  zy,
  input  ny,
  input  [15:0] x,
  input  [15:0] y,
  input  no,
  output [15:0] out,
  output zr,
  output ng
);

  wire or_1_out, or_2_out, or_3_out;
  wire [15:0] adder_16_1_sum, and_1_out, multiplexer_1_out, multiplexer_2_out, multiplexer_3_out,
       multiplexer_4_out, multiplexer_5_out, not_1_out, not_2_out, not_3_out;

  Multiplexer #(.Bits(16)) multiplexer_1 (.sel(zx), .in_0(x), .in_1({16{1'b0}}), .out(multiplexer_1_out));
  Multiplexer #(.Bits(16)) multiplexer_2 (
    .sel(nx), .in_0(multiplexer_1_out), .in_1(not_1_out), .out(multiplexer_2_out));
  Multiplexer #(.Bits(16)) multiplexer_3 (.sel(zy), .in_0(y), .in_1({16{1'b0}}), .out(multiplexer_3_out));
  Multiplexer #(.Bits(16)) multiplexer_4 (
    .sel(ny), .in_0(multiplexer_3_out), .in_1(not_2_out), .out(multiplexer_4_out));
  assign not_1_out = ~multiplexer_1_out;  // Not not_1, 16 bits wide
  assign not_2_out = ~multiplexer_3_out;  // Not not_2, 16 bits wide
  assign and_1_out = multiplexer_2_out & multiplexer_4_out;  // And and_1, 16 bits wide
  adder_16 adder_16_1 (.a(multiplexer_2_out), .b(multiplexer_4_out), .sum(adder_16_1_sum));
  Multiplexer #(.Bits(16)) multiplexer_5 (.sel(f), .in_0(and_1_out), .in_1(adder_16_1_sum), .out(multiplexer_5_out));
  assign not_3_out = ~multiplexer_5_out;  // Not not_3, 16 bits wide
  Multiplexer #(.Bits(16)) multiplexer_6 (.sel(no), .in_0(multiplexer_5_out), .in_1(not_3_out), .out({ng, out[14:0]}));
  or or_1 (or_1_out, out[0], out[1], out[2], out[3], out[4], out[5], out[6], out[7]);
  or or_2 (or_2_out, out[8], out[9], out[10], out[11], out[12], out[13], out[14], ng);
  or or_3 (or_3_out, or_1_out, or_2_out);
  not not_4 (zr, or_3_out);

  assign out[15] = ng;
endmodule
