// Digital circuit full_adder.dig as structural Verilog
module full_adder (
  input  a,
  input  b,
  input  c,
  output sum,
  output carry
);

  wire half_adder_1_carry, half_adder_1_sum, half_adder_2_carry;

  Half_adder half_adder_1 (.a(a), .b(b), .carry(half_adder_1_carry), .sum(half_adder_1_sum));
  Half_adder half_adder_2 (.a(c), .b(half_adder_1_sum), .carry(half_adder_2_carry), .sum(sum));
  or or_1 (carry, half_adder_1_carry, half_adder_2_carry);
endmodule
