// Digital circuit pc_16.dig as structural Verilog
module pc_16 (
  input  [15:0] in,
  input  load,
  input  inc,
  input  reset,
  input  clk,
  output [15:0] out
);

  wire or_1_out;
  wire [15:0] incrementer_16_1_sum, mux16_1_out, mux16_2_out;

  or or_1 (or_1_out, load, reset, inc);
  mux16 mux16_1 (.a(in), .b(incrementer_16_1_sum), .sel(inc), .out(mux16_1_out));
  mux16 mux16_2 (.a(mux16_1_out), .b({16{1'b0}}), .sel(reset), .out(mux16_2_out));
  register_16 register_16_1 (.clk(clk), .load(or_1_out), .in(mux16_2_out), .out(out));
  incrementer_16 incrementer_16_1 (.a(out), .sum(incrementer_16_1_sum));
endmodule
