// Digital circuit ram4096.dig as structural Verilog
module ram4096 (
  input  [11:0] addr,
  input  clk,
  input  [15:0] in,
  input  load,
  output [15:0] out
);

  wire _8waydmux_1_a, _8waydmux_1_b, _8waydmux_1_c, _8waydmux_1_d, _8waydmux_1_e, _8waydmux_1_f,
       _8waydmux_1_g, _8waydmux_1_h;
  wire [15:0] ram512_1_out, ram512_2_out, ram512_3_out, ram512_4_out, ram512_5_out, ram512_6_out,
       ram512_7_out, ram512_8_out;

  _8wayDmux _8waydmux_1 (
    .in(load), .sel(addr[2:0]), .a(_8waydmux_1_a), .b(_8waydmux_1_b), .c(_8waydmux_1_c), .d(_8waydmux_1_d),
    .e(_8waydmux_1_e), .f(_8waydmux_1_f), .g(_8waydmux_1_g), .h(_8waydmux_1_h));
  ram512 ram512_1 (.in(in), .load(_8waydmux_1_a), .addr(addr[11:3]), .clk(clk), .out(ram512_1_out));
  ram512 ram512_2 (.in(in), .load(_8waydmux_1_b), .addr(addr[11:3]), .clk(clk), .out(ram512_2_out));
  ram512 ram512_3 (.in(in), .load(_8waydmux_1_c), .addr(addr[11:3]), .clk(clk), .out(ram512_3_out));
  ram512 ram512_4 (.in(in), .load(_8waydmux_1_d), .addr(addr[11:3]), .clk(clk), .out(ram512_4_out));
  ram512 ram512_5 (.in(in), .load(_8waydmux_1_e), .addr(addr[11:3]), .clk(clk), .out(ram512_5_out));
  ram512 ram512_6 (.in(in), .load(_8waydmux_1_f), .addr(addr[11:3]), .clk(clk), .out(ram512_6_out));
  ram512 ram512_7 (.in(in), .load(_8waydmux_1_g), .addr(addr[11:3]), .clk(clk), .out(ram512_7_out));
  ram512 ram512_8 (.in(in), .load(_8waydmux_1_h), .addr(addr[11:3]), .clk(clk), .out(ram512_8_out));
  _8waymux16 _8waymux16_1 (
    .a(ram512_1_out), .b(ram512_2_out), .c(ram512_3_out), .d(ram512_4_out), .e(ram512_5_out),
    .f(ram512_6_out), .g(ram512_7_out), .h(ram512_8_out), .sel(addr[2:0]), .out(out));
endmodule
