// Digital circuit ram512.dig as structural Verilog
module ram512 (
  input  [15:0] in,
  input  load,
  input  [8:0] addr,
  input  clk,
  output [15:0] out
);

  wire _8waydmux_1_a, _8waydmux_1_b, _8waydmux_1_c, _8waydmux_1_d, _8waydmux_1_e, _8waydmux_1_f,
       _8waydmux_1_g, _8waydmux_1_h;
  wire [15:0] ram64_1_out, ram64_2_out, ram64_3_out, ram64_4_out, ram64_5_out, ram64_6_out, ram64_7_out,
       ram64_8_out;

  _8wayDmux _8waydmux_1 (
    .in(load), .sel(addr[2:0]), .a(_8waydmux_1_a), .b(_8waydmux_1_b), .c(_8waydmux_1_c), .d(_8waydmux_1_d),
    .e(_8waydmux_1_e), .f(_8waydmux_1_f), .g(_8waydmux_1_g), .h(_8waydmux_1_h));
  ram64 ram64_1 (.in(in), .load(_8waydmux_1_a), .addr(addr[8:3]), .clk(clk), .out(ram64_1_out));
  ram64 ram64_2 (.in(in), .load(_8waydmux_1_b), .addr(addr[8:3]), .clk(clk), .out(ram64_2_out));
  ram64 ram64_3 (.in(in), .load(_8waydmux_1_c), .addr(addr[8:3]), .clk(clk), .out(ram64_3_out));
  ram64 ram64_4 (.in(in), .load(_8waydmux_1_d), .addr(addr[8:3]), .clk(clk), .out(ram64_4_out));
  ram64 ram64_5 (.in(in), .load(_8waydmux_1_e), .addr(addr[8:3]), .clk(clk), .out(ram64_5_out));
  ram64 ram64_6 (.in(in), .load(_8waydmux_1_f), .addr(addr[8:3]), .clk(clk), .out(ram64_6_out));
  ram64 ram64_7 (.in(in), .load(_8waydmux_1_g), .addr(addr[8:3]), .clk(clk), .out(ram64_7_out));
  ram64 ram64_8 (.in(in), .load(_8waydmux_1_h), .addr(addr[8:3]), .clk(clk), .out(ram64_8_out));
  _8waymux16 _8waymux16_1 (
    .a(ram64_1_out), .b(ram64_2_out), .c(ram64_3_out), .d(ram64_4_out), .e(ram64_5_out), .f(ram64_6_out),
    .g(ram64_7_out), .h(ram64_8_out), .sel(addr[2:0]), .out(out));
endmodule
