// Digital circuit ram64.dig as structural Verilog
module ram64 (
  input  [15:0] in,
  input  load,
  input  [5:0] addr,
  input  clk,
  output [15:0] out
);

  wire _8waydmux_1_a, _8waydmux_1_b, _8waydmux_1_c, _8waydmux_1_d, _8waydmux_1_e, _8waydmux_1_f,
       _8waydmux_1_g, _8waydmux_1_h;
  wire [15:0] ram8_1_out, ram8_2_out, ram8_3_out, ram8_4_out, ram8_5_out, ram8_6_out, ram8_7_out, ram8_8_out;

  _8wayDmux _8waydmux_1 (
    .in(load), .sel(addr[2:0]), .a(_8waydmux_1_a), .b(_8waydmux_1_b), .c(_8waydmux_1_c), .d(_8waydmux_1_d),
    .e(_8waydmux_1_e), .f(_8waydmux_1_f), .g(_8waydmux_1_g), .h(_8waydmux_1_h));
  ram8 ram8_1 (.in(in), .load(_8waydmux_1_a), .addr(addr[5:3]), .clk(clk), .out(ram8_1_out));
  ram8 ram8_2 (.in(in), .load(_8waydmux_1_b), .addr(addr[5:3]), .clk(clk), .out(ram8_2_out));
  ram8 ram8_3 (.in(in), .load(_8waydmux_1_c), .addr(addr[5:3]), .clk(clk), .out(ram8_3_out));
  ram8 ram8_4 (.in(in), .load(_8waydmux_1_d), .addr(addr[5:3]), .clk(clk), .out(ram8_4_out));
  ram8 ram8_5 (.in(in), .load(_8waydmux_1_e), .addr(addr[5:3]), .clk(clk), .out(ram8_5_out));
  ram8 ram8_6 (.in(in), .load(_8waydmux_1_f), .addr(addr[5:3]), .clk(clk), .out(ram8_6_out));
  ram8 ram8_7 (.in(in), .load(_8waydmux_1_g), .addr(addr[5:3]), .clk(clk), .out(ram8_7_out));
  ram8 ram8_8 (.in(in), .load(_8waydmux_1_h), .addr(addr[5:3]), .clk(clk), .out(ram8_8_out));
  _8waymux16 _8waymux16_1 (
    .a(ram8_1_out), .b(ram8_2_out), .c(ram8_3_out), .d(ram8_4_out), .e(ram8_5_out), .f(ram8_6_out),
    .g(ram8_7_out), .h(ram8_8_out), .sel(addr[2:0]), .out(out));
endmodule
