// Digital circuit ram8.dig as structural Verilog
module ram8 (
  input  [15:0] in,
  input  load,
  input  [2:0] addr,
  input  clk,
  output [15:0] out
);

  wire _8waydmux_1_a, _8waydmux_1_b, _8waydmux_1_c, _8waydmux_1_d, _8waydmux_1_e, _8waydmux_1_f,
       _8waydmux_1_g, _8waydmux_1_h;
  wire [15:0] register_16_1_out, register_16_2_out, register_16_3_out, register_16_4_out, register_16_5_out,
       register_16_6_out, register_16_7_out, register_16_8_out;

  _8wayDmux _8waydmux_1 (
    .in(load), .sel(addr), .a(_8waydmux_1_a), .b(_8waydmux_1_b), .c(_8waydmux_1_c), .d(_8waydmux_1_d),
    .e(_8waydmux_1_e), .f(_8waydmux_1_f), .g(_8waydmux_1_g), .h(_8waydmux_1_h));
  register_16 register_16_1 (.clk(clk), .load(_8waydmux_1_a), .in(in), .out(register_16_1_out));
  register_16 register_16_2 (.clk(clk), .load(_8waydmux_1_b), .in(in), .out(register_16_2_out));
  register_16 register_16_3 (.clk(clk), .load(_8waydmux_1_c), .in(in), .out(register_16_3_out));
  register_16 register_16_4 (.clk(clk), .load(_8waydmux_1_d), .in(in), .out(register_16_4_out));
  register_16 register_16_5 (.clk(clk), .load(_8waydmux_1_e), .in(in), .out(register_16_5_out));
  register_16 register_16_6 (.clk(clk), .load(_8waydmux_1_f), .in(in), .out(register_16_6_out));
  register_16 register_16_7 (.clk(clk), .load(_8waydmux_1_g), .in(in), .out(register_16_7_out));
  register_16 register_16_8 (.clk(clk), .load(_8waydmux_1_h), .in(in), .out(register_16_8_out));
  _8waymux16 _8waymux16_1 (
    .a(register_16_1_out), .b(register_16_2_out), .c(register_16_3_out), .d(register_16_4_out),
    .e(register_16_5_out), .f(register_16_6_out), .g(register_16_7_out), .h(register_16_8_out), .sel(addr),
    .out(out));
endmodule
