// Digital circuit register_16.dig as structural Verilog
module register_16 (
  input  clk,
  input  load,
  input  [15:0] in,
  output [15:0] out
);

  _1_bit _1_bit_1 (.clk(clk), .load(load), .in(in[0]), .out(out[0]));
  _1_bit _1_bit_2 (.clk(clk), .load(load), .in(in[1]), .out(out[1]));
  _1_bit _1_bit_3 (.clk(clk), .load(load), .in(in[2]), .out(out[2]));
  _1_bit _1_bit_4 (.clk(clk), .load(load), .in(in[3]), .out(out[3]));
  _1_bit _1_bit_5 (.clk(clk), .load(load), .in(in[4]), .out(out[4]));
  _1_bit _1_bit_6 (.clk(clk), .load(load), .in(in[5]), .out(out[5]));
  _1_bit _1_bit_7 (.clk(clk), .load(load), .in(in[6]), .out(out[6]));
  _1_bit _1_bit_8 (.clk(clk), .load(load), .in(in[7]), .out(out[7]));
  _1_bit _1_bit_9 (.clk(clk), .load(load), .in(in[8]), .out(out[8]));
  _1_bit _1_bit_10 (.clk(clk), .load(load), .in(in[9]), .out(out[9]));
  _1_bit _1_bit_11 (.clk(clk), .load(load), .in(in[10]), .out(out[10]));
  _1_bit _1_bit_12 (.clk(clk), .load(load), .in(in[11]), .out(out[11]));
  _1_bit _1_bit_13 (.clk(clk), .load(load), .in(in[12]), .out(out[12]));
  _1_bit _1_bit_14 (.clk(clk), .load(load), .in(in[13]), .out(out[13]));
  _1_bit _1_bit_15 (.clk(clk), .load(load), .in(in[14]), .out(out[14]));
  _1_bit _1_bit_16 (.clk(clk), .load(load), .in(in[15]), .out(out[15]));
endmodule
